# Fritzing sketch diagram (saved by Fritzing 0.8.7b)
breadboards: 1

parts:
  Part1 = Arduino Uno (Rev3)
  S1 = Pushbutton [package="[THT]"]
  R1 = Resistor [tolerance=±5% resistance=220 package=THT]
  LED1 = LED - 5mm [color="Red (633nm)" package="5 mm [THT]"]
  R2 = Resistor [tolerance=±5% resistance=220 package=THT]

nets:
  N1: Part1.D13/SCK, R2.Pin_0
  N2: Part1.D2, S1.Pin_1, S1.Pin_2, R1.Pin_0
  N3: Part1.3V3, R1.Pin_1
  N4: Part1.GND, S1.Pin_3, S1.Pin_4, LED1.anode
  N5: LED1.cathode, R2.Pin_1
